# Fritzing sketch diagram (saved by Fritzing 0.9.10b)
breadboards: 2

parts:
  Part6 = Arduino Nano (Rev3.0) [part_number=1]
  LED5 = LED - 5mm [color="Green (560nm)" current=0.030 package="5 mm [THT]"]
  C2 = Electrolytic Capacitor [capacitance=10µF voltage=16V package="0807 [SMD, electrolytic]"]
  R11 = Resistor [tolerance=±5% power=0.25 resistance=220 package=THT]
  LED6 = LED - 5mm [color="Red (633nm)" current=0.030 package="5 mm [THT]"]
  R7 = Resistor [tolerance=±5% power=0.25 resistance=220 package=THT]
  Part5 = NRF24L01+ Breakout Board
  R10 = Resistor [tolerance=±5% power=0.25 resistance=220 package=THT]
  SP2 = SPEAKER [package=pcb_mount_speaker]
  VCC2 = 4 x AAA Battery Mount
  R9 = Resistor [tolerance=±5% power=0.25W resistance=1k package=THT]
  LED7 = LED - 5mm [color="Yellow (595nm)" current=0.030 package="5 mm [THT]"]
  R8 = Resistor [tolerance=±5% power=0.25 resistance=2.2k package=THT]
  Part1 = MQ-3 breakout
  R2 = Resistor [tolerance=±5% power=0.25 resistance=2.2k package=THT]
  R1 = Resistor [tolerance=±5% power=0.25W resistance=1k package=THT]
  R14 = Resistor [tolerance=±5% power=0.25 resistance=220 package=THT]
  part = Resistor [tolerance=±5% power=0.25 resistance=220 package=THT]
  R16 = Resistor [tolerance=±5% power=0.25 resistance=220 package=THT]
  LED8 = LED - 5mm [color="Yellow (595nm)" current=0.030 package="5 mm [THT]"]
  LED9 = LED - 5mm [color="Red (633nm)" current=0.030 package="5 mm [THT]"]
  LED10 = LED - 5mm [color="Green (560nm)" current=0.030 package="5 mm [THT]"]
  C1 = Electrolytic Capacitor [capacitance=10µF voltage=16V package="0807 [SMD, electrolytic]"]
  Part7 = NRF24L01+ Breakout Board
  Part8 = Arduino Nano (Rev3.0) [part_number=1]
  SP3 = SPEAKER [package=pcb_mount_speaker]
  VCC3 = 4 x AAA Battery Mount

nets:
  GND: Part6.GND, C2.-, Part5.GND, VCC2.-
  N1: Part6.D2, LED5.anode, R11.Pin_0, R11.Pin_1
  N2: Part6.D3, R10.Pin_0, R10.Pin_1, LED7.anode
  N3: Part6.D4, LED6.anode, R7.Pin_0, R7.Pin_1
  N4: Part6.D5, SP2.-
  N5: Part6.D7, Part5.CE
  N6: Part6.D8, Part5.CS
  N7: Part6.D11/MOSI, Part5.MOSI
  N8: Part6.D12/MISO, Part5.MISO
  N9: Part6.VIN, VCC2.+, R9.Pin_0
  N10: Part6.D13/SCK, Part5.SCK
  N11: LED5.cathode, LED6.cathode, SP2.+, LED7.cathode
  N12: C2.+, Part5.VCC, R8.Pin_1
  N13: R9.Pin_1, R8.Pin_0
  VCC: Part1.VCC, Part8.5V
  GND_2: Part1.GND, LED8.cathode, LED9.cathode, LED10.cathode, C1.-, Part7.GND, Part8.GND, SP3.+, VCC3.-
  N14: Part1.AO, Part8.A7
  N15: R2.Pin_0, R1.Pin_1
  N16: R2.Pin_1, C1.+, Part7.VCC
  N17: R1.Pin_0, Part8.VIN, VCC3.+
  N18: R14.Pin_0, R14.Pin_1, LED8.anode, Part8.D3
  N19: part.Pin_0, part.Pin_1, LED9.anode, Part8.D4
  N20: R16.Pin_0, R16.Pin_1, LED10.anode, Part8.D2
  N21: Part7.CE, Part8.D7
  N22: Part7.CS, Part8.D8
  N23: Part7.SCK, Part8.D13/SCK
  N24: Part7.MOSI, Part8.D11/MOSI
  N25: Part7.MISO, Part8.D12/MISO
  N26: Part8.D5, SP3.-

notes:
  Sensor unit
  Central unit

custom parts:
  MQ-3 breakout: Alcohol sensor is capable of detecting alcohol (ethanol) particles on itself and gives the information in digital form back to us to manipulate with it. SKU:101251 • Voltage: 5V DC • Power: max 750mW • Measurement range: 0.04-4mg/L
