# Fritzing sketch schema (saved by Fritzing 0.9.10b)

parts:
  Part10 = Arduino Nano (Rev3.0)
  SP4 = SPEAKER [package=pcb_mount_speaker]
  LED10 = smd LED [color="Green (570nm)" package="0603 [SMD]"]
  LED11 = smd LED [color="Red (633nm)" package="0603 [SMD]"]
  LED12 = smd LED [color="Yellow (595nm)" package="0805 [SMD]"]
  R14 = Resistor [tolerance=±5% resistance=220 package="0805 [SMD]"]
  R15 = Resistor [tolerance=±5% resistance=220 package="0805 [SMD]"]
  R16 = Resistor [tolerance=±5% resistance=220 package="0805 [SMD]"]
  Part11 = NRF24L01+ Breakout Board
  C5 = Electrolytic Capacitor [capacitance=10µF voltage=16V package="0807 [SMD, electrolytic]"]
  VCC5 = 4 x AAA Battery Mount
  Part12 = Arduino Nano (Rev3.0)
  SP5 = SPEAKER [package=pcb_mount_speaker]
  LED13 = smd LED [color="Yellow (595nm)" package="0805 [SMD]"]
  LED14 = smd LED [color="Green (570nm)" package="0603 [SMD]"]
  LED15 = smd LED [color="Red (633nm)" package="0603 [SMD]"]
  R17 = Resistor [tolerance=±5% resistance=220 package="0805 [SMD]"]
  R18 = Resistor [tolerance=±5% resistance=220 package="0805 [SMD]"]
  R19 = Resistor [tolerance=±5% resistance=220 package="0805 [SMD]"]
  Part13 = NRF24L01+ Breakout Board
  C6 = Electrolytic Capacitor [capacitance=10µF voltage=16V package="0807 [SMD, electrolytic]"]
  VCC6 = 4 x AAA Battery Mount
  Part14 = MQ-3 breakout

nets:
  GND: Part10.GND, SP4.-, LED10.cathode, LED11.cathode, LED12.cathode, Part11.GND, C5.-, VCC5.-
  N1: Part10.D2, R16.Pin_0
  N2: Part10.D3, R15.Pin_0
  N3: Part10.D4, R14.Pin_0
  N4: Part10.D8, SP4.+
  N5: Part10.D9, Part11.CS
  N6: Part10.D10, Part11.CE
  N7: Part10.D11/MOSI, Part11.MOSI
  N8: Part10.D12/MISO, Part11.MISO
  N9: Part10.VIN, VCC5.+
  3V3: Part10.3V3, Part11.VCC, C5.+
  N10: Part10.D13/SCK, Part11.SCK
  N11: LED10.anode, R16.Pin_1
  N12: LED11.anode, R14.Pin_1
  N13: LED12.anode, R15.Pin_1
  GND_2: Part12.GND, SP5.-, LED13.cathode, LED14.cathode, LED15.cathode, Part13.GND, C6.-, VCC6.-, Part14.GND
  N14: Part12.D2, R19.Pin_0
  N15: Part12.D3, R18.Pin_0
  N16: Part12.D4, R17.Pin_0
  N17: Part12.D7, SP5.+
  N18: Part12.D8, Part14.DO
  N19: Part12.D9, Part13.CS
  N20: Part12.D10, Part13.CE
  N21: Part12.D11/MOSI, Part13.MOSI
  N22: Part12.D12/MISO, Part13.MISO
  N23: Part12.VIN, VCC6.+
  5V: Part12.5V, Part14.VCC
  3V3_2: Part12.3V3, Part13.VCC, C6.+
  N24: Part12.D13/SCK, Part13.SCK
  N25: LED13.anode, R18.Pin_1
  N26: LED14.anode, R19.Pin_1
  N27: LED15.anode, R17.Pin_1

custom parts:
  MQ-3 breakout: Alcohol sensor is capable of detecting alcohol (ethanol) particles on itself and gives the information in digital form back to us to manipulate with it. SKU:101251 • Voltage: 5V DC • Power: max 750mW • Measurement range: 0.04-4mg/L
